// Logisim project aois_lab3.circ as structural Verilog
// bit
module _1_bit_Summer (
  input  x1,
  input  x2,
  input  x3,
  output d,
  output bout
);

  wire and_1_out, and_2_out, and_3_out, and_4_out, and_5_out, and_6_out, and_7_out, not_1_out, not_2_out,
       not_3_out, not_4_out, not_5_out, not_6_out, not_7_out, not_8_out;

  not not_1 (not_1_out, x2);
  not not_2 (not_2_out, x3);
  not not_3 (not_3_out, x1);
  not not_4 (not_4_out, x3);
  not not_5 (not_5_out, x1);
  not not_6 (not_6_out, x2);
  not not_7 (not_7_out, x1);
  not not_8 (not_8_out, x1);
  and and_1 (and_1_out, x1, x2, x3);
  and and_2 (and_2_out, x1, not_1_out, not_2_out);
  and and_3 (and_3_out, x2, not_3_out, not_4_out);
  and and_4 (and_4_out, x3, not_5_out, not_6_out);
  and and_5 (and_5_out, x2, x3);
  and and_6 (and_6_out, x2, not_7_out);
  and and_7 (and_7_out, x3, not_8_out);
  or or_1 (d, and_1_out, and_2_out, and_3_out, and_4_out);
  or or_2 (bout, and_5_out, and_6_out, and_7_out);
endmodule

module digital_machine (
  input  V,
  input  V_2
);

  wire and_1_out, and_2_out, and_3_out, clock_1_out, clock_2_out, q1_qn, q2_qn, q3_qn;
  wire [3:0] q1_q;

  Clock clock_1 (.out(clock_1_out));
  T_Flip_Flop q1 (.clk(clock_1_out), .T(V), .Q(q1_q[0]), .Qn(q1_qn));  // open: preset, reset, en
  and and_1 (and_1_out, q1_qn, V);
  Clock clock_2 (.out(clock_2_out));
  T_Flip_Flop q2 (.clk(clock_1_out), .T(and_1_out), .Q(q1_q[1]), .Qn(q2_qn));  // open: preset, reset, en
  and and_2 (and_2_out, and_1_out, q2_qn);
  D_Flip_Flop d_ff_1 (.clk(clock_2_out), .D(V_2));  // open: Q, Qn, preset, en, reset
  T_Flip_Flop q3 (.clk(clock_1_out), .T(and_2_out), .Q(q1_q[2]), .Qn(q3_qn));  // open: preset, reset, en
  J_K_Flip_Flop j_k_ff_1 ();  // open: J, clk, K, Q, Qn, preset, en, reset
  S_R_Flip_Flop s_r_ff_1 ();  // open: S, clk, R, Q, Qn, preset, reset, en
  and and_3 (and_3_out, and_2_out, q3_qn);
  T_Flip_Flop q4 (.clk(clock_1_out), .T(and_3_out), .Q(q1_q[3]));  // open: Qn, preset, reset, en
  Hex_Digit_Display hex_digit_display_1 (.value(q1_q));  // open: dp
endmodule

module combinational_circuit (
  input  a3,
  input  a2,
  input  a1,
  input  a0,
  input  b3,
  input  b2,
  input  b1,
  input  b0,
  output y1_3,
  output y1_2,
  output y1_1,
  output y1_0,
  output y0_3,
  output y0_2,
  output y0_1,
  output y0_0
);

  wire and_1_out, and_2_out, and_3_out, and_4_out, and_5_out, and_6_out, and_7_out, and_8_out, and_9_out,
       and_10_out, and_11_out, and_12_out, and_13_out, and_14_out, and_15_out, and_16_out, and_17_out,
       and_18_out, and_19_out, and_20_out, and_21_out, and_22_out, and_23_out, and_24_out, and_25_out,
       and_26_out, and_27_out, and_28_out, and_29_out, and_30_out, and_31_out, and_32_out, and_33_out,
       and_34_out, and_35_out, and_36_out, and_37_out, and_38_out, and_39_out, and_40_out, and_41_out,
       and_42_out, and_43_out, and_44_out, and_45_out, and_46_out, and_47_out, and_48_out, and_49_out,
       and_50_out, and_51_out, and_52_out, and_53_out, and_54_out, and_55_out, and_56_out, and_57_out,
       and_58_out, and_59_out, and_60_out, and_61_out, and_62_out, and_63_out, and_64_out, and_65_out,
       and_66_out, and_67_out, and_68_out, and_69_out, and_70_out, and_71_out, and_72_out, and_73_out,
       and_74_out, and_75_out, and_76_out, and_77_out, and_78_out, and_79_out, and_80_out, and_81_out,
       and_82_out, and_83_out, and_84_out, and_85_out, and_86_out, and_87_out, and_88_out, and_89_out,
       and_90_out, not_1_out, not_2_out, not_3_out, not_4_out, not_5_out, not_6_out, not_7_out, not_8_out,
       not_9_out, not_10_out, not_11_out, not_12_out, not_13_out, not_14_out, not_15_out, not_16_out,
       not_17_out, not_18_out, not_19_out, not_20_out, not_21_out, not_22_out, not_23_out, not_24_out,
       not_25_out, not_26_out, not_27_out, not_28_out, not_29_out, not_30_out, not_31_out, not_32_out,
       not_33_out, not_34_out, not_35_out, not_36_out, not_37_out, not_38_out, not_39_out, not_40_out,
       not_41_out, not_42_out, not_43_out, not_44_out, not_45_out, not_46_out, not_47_out, not_48_out,
       not_49_out, not_50_out, not_51_out, not_52_out, not_53_out, not_54_out, not_55_out, not_56_out,
       not_57_out, not_58_out, not_59_out, not_60_out, not_61_out, not_62_out, not_63_out, not_64_out,
       not_65_out, not_66_out, not_67_out, not_68_out, not_69_out, not_70_out, not_71_out, not_72_out,
       not_73_out, not_74_out, not_75_out, not_76_out, not_77_out, not_78_out, not_79_out, not_80_out,
       not_81_out, not_82_out, not_83_out, not_84_out, not_85_out, not_86_out, not_87_out, not_88_out,
       not_89_out, not_90_out, not_91_out, not_92_out, not_93_out, not_94_out, not_95_out, not_96_out,
       not_97_out, not_98_out, not_99_out, not_100_out, not_101_out, not_102_out, not_103_out, not_104_out,
       not_105_out, not_106_out, not_107_out, not_108_out, not_109_out, not_110_out, not_111_out,
       not_112_out, not_113_out, not_114_out, not_115_out, not_116_out, not_117_out, not_118_out,
       not_119_out, not_120_out, not_121_out, not_122_out, not_123_out, not_124_out, not_125_out,
       not_126_out, not_127_out, not_128_out, not_129_out, not_130_out, not_131_out, not_132_out,
       not_133_out, not_134_out, not_135_out, not_136_out, not_137_out, not_138_out, not_139_out,
       not_140_out, not_141_out, not_142_out, not_143_out, not_144_out, not_145_out, not_146_out,
       not_147_out, not_148_out, not_149_out, not_150_out, not_151_out, not_152_out, not_153_out,
       not_154_out, not_155_out, not_156_out, not_157_out, not_158_out, not_159_out, not_160_out,
       not_161_out, not_162_out, not_163_out, not_164_out, not_165_out, not_166_out, not_167_out,
       not_168_out, not_169_out, not_170_out, not_171_out, not_172_out, not_173_out, not_174_out,
       not_175_out, not_176_out, not_177_out, not_178_out, not_179_out, not_180_out, not_181_out,
       not_182_out, not_183_out, not_184_out, not_185_out, not_186_out, not_187_out, not_188_out,
       not_189_out, not_190_out, not_191_out, not_192_out, not_193_out, not_194_out, not_195_out,
       not_196_out, not_197_out, not_198_out, not_199_out, not_200_out, not_201_out, not_202_out,
       not_203_out, not_204_out, not_205_out, not_206_out, not_207_out, not_208_out;

  and and_1 (and_1_out, a0, a1, a2, b2);
  and and_2 (and_2_out, a0, a2, b1, b2);
  and and_3 (and_3_out, a1, a2, b0, b2);
  and and_4 (and_4_out, a1, a2, b1, b2);
  and and_5 (and_5_out, a2, b0, b1, b2);
  not not_1 (not_1_out, a2);
  not not_2 (not_2_out, a3);
  not not_3 (not_3_out, b3);
  not not_4 (not_4_out, a3);
  not not_5 (not_5_out, b2);
  not not_6 (not_6_out, b3);
  not not_7 (not_7_out, a1);
  not not_8 (not_8_out, a3);
  not not_9 (not_9_out, b1);
  not not_10 (not_10_out, b3);
  not not_11 (not_11_out, a0);
  not not_12 (not_12_out, a1);
  not not_13 (not_13_out, a3);
  not not_14 (not_14_out, b0);
  not not_15 (not_15_out, b3);
  not not_16 (not_16_out, a0);
  not not_17 (not_17_out, a3);
  not not_18 (not_18_out, b0);
  not not_19 (not_19_out, b1);
  not not_20 (not_20_out, b3);
  not not_21 (not_21_out, a2);
  not not_22 (not_22_out, a3);
  not not_23 (not_23_out, b3);
  not not_24 (not_24_out, a3);
  not not_25 (not_25_out, b2);
  not not_26 (not_26_out, b3);
  not not_27 (not_27_out, a1);
  not not_28 (not_28_out, a3);
  not not_29 (not_29_out, b1);
  not not_30 (not_30_out, b3);
  not not_31 (not_31_out, a0);
  not not_32 (not_32_out, a1);
  not not_33 (not_33_out, a3);
  not not_34 (not_34_out, b0);
  not not_35 (not_35_out, b3);
  not not_36 (not_36_out, a0);
  not not_37 (not_37_out, a3);
  not not_38 (not_38_out, b0);
  not not_39 (not_39_out, b1);
  not not_40 (not_40_out, b3);
  not not_41 (not_41_out, b2);
  not not_42 (not_42_out, a2);
  not not_43 (not_43_out, b3);
  not not_44 (not_44_out, a3);
  not not_45 (not_45_out, a2);
  not not_46 (not_46_out, a3);
  not not_47 (not_47_out, b3);
  not not_48 (not_48_out, a3);
  not not_49 (not_49_out, b2);
  not not_50 (not_50_out, b3);
  not not_51 (not_51_out, b2);
  not not_52 (not_52_out, b1);
  not not_53 (not_53_out, a2);
  not not_54 (not_54_out, a1);
  not not_55 (not_55_out, a2);
  not not_56 (not_56_out, b1);
  not not_57 (not_57_out, b2);
  not not_58 (not_58_out, b0);
  not not_59 (not_59_out, b1);
  not not_60 (not_60_out, b2);
  not not_61 (not_61_out, a1);
  not not_62 (not_62_out, a3);
  not not_63 (not_63_out, b1);
  not not_64 (not_64_out, a0);
  not not_65 (not_65_out, a1);
  not not_66 (not_66_out, a2);
  not not_67 (not_67_out, a1);
  not not_68 (not_68_out, a2);
  not not_69 (not_69_out, b2);
  not not_70 (not_70_out, a0);
  not not_71 (not_71_out, a2);
  not not_72 (not_72_out, b0);
  not not_73 (not_73_out, b2);
  not not_74 (not_74_out, a0);
  not not_75 (not_75_out, a3);
  not not_76 (not_76_out, b0);
  not not_77 (not_77_out, b1);
  not not_78 (not_78_out, a0);
  not not_79 (not_79_out, a1);
  not not_80 (not_80_out, a3);
  not not_81 (not_81_out, b0);
  not not_82 (not_82_out, b3);
  not not_83 (not_83_out, a2);
  not not_84 (not_84_out, b2);
  not not_85 (not_85_out, a0);
  not not_86 (not_86_out, b2);
  not not_87 (not_87_out, b3);
  not not_88 (not_88_out, a2);
  not not_89 (not_89_out, a3);
  not not_90 (not_90_out, b3);
  not not_91 (not_91_out, a2);
  not not_92 (not_92_out, b2);
  not not_93 (not_93_out, a3);
  not not_94 (not_94_out, b0);
  not not_95 (not_95_out, b1);
  not not_96 (not_96_out, b2);
  not not_97 (not_97_out, a0);
  not not_98 (not_98_out, a1);
  not not_99 (not_99_out, a2);
  not not_100 (not_100_out, a0);
  not not_101 (not_101_out, a2);
  not not_102 (not_102_out, b1);
  not not_103 (not_103_out, b3);
  not not_104 (not_104_out, a0);
  not not_105 (not_105_out, a3);
  not not_106 (not_106_out, b1);
  not not_107 (not_107_out, b2);
  not not_108 (not_108_out, a1);
  not not_109 (not_109_out, a2);
  not not_110 (not_110_out, b0);
  not not_111 (not_111_out, b3);
  not not_112 (not_112_out, a1);
  not not_113 (not_113_out, a3);
  not not_114 (not_114_out, b0);
  not not_115 (not_115_out, b2);
  not not_116 (not_116_out, a1);
  not not_117 (not_117_out, a3);
  not not_118 (not_118_out, b1);
  not not_119 (not_119_out, a1);
  not not_120 (not_120_out, b1);
  not not_121 (not_121_out, b3);
  not not_122 (not_122_out, a0);
  not not_123 (not_123_out, a3);
  not not_124 (not_124_out, b0);
  not not_125 (not_125_out, b3);
  not not_126 (not_126_out, a2);
  not not_127 (not_127_out, b0);
  not not_128 (not_128_out, b1);
  not not_129 (not_129_out, b3);
  not not_130 (not_130_out, a0);
  not not_131 (not_131_out, a3);
  not not_132 (not_132_out, b0);
  not not_133 (not_133_out, b3);
  not not_134 (not_134_out, a0);
  not not_135 (not_135_out, a1);
  not not_136 (not_136_out, a3);
  not not_137 (not_137_out, b2);
  not not_138 (not_138_out, a0);
  not not_139 (not_139_out, a2);
  not not_140 (not_140_out, b0);
  not not_141 (not_141_out, b2);
  not not_142 (not_142_out, a1);
  not not_143 (not_143_out, b0);
  not not_144 (not_144_out, a0);
  not not_145 (not_145_out, b1);
  not not_146 (not_146_out, b0);
  not not_147 (not_147_out, b1);
  not not_148 (not_148_out, b2);
  not not_149 (not_149_out, a0);
  not not_150 (not_150_out, a1);
  not not_151 (not_151_out, a2);
  not not_152 (not_152_out, b0);
  not not_153 (not_153_out, b2);
  not not_154 (not_154_out, a1);
  not not_155 (not_155_out, a2);
  not not_156 (not_156_out, b1);
  not not_157 (not_157_out, b2);
  not not_158 (not_158_out, a0);
  not not_159 (not_159_out, a2);
  not not_160 (not_160_out, b3);
  not not_161 (not_161_out, a3);
  not not_162 (not_162_out, b0);
  not not_163 (not_163_out, b1);
  not not_164 (not_164_out, b3);
  not not_165 (not_165_out, a1);
  not not_166 (not_166_out, a2);
  not not_167 (not_167_out, b1);
  not not_168 (not_168_out, a1);
  not not_169 (not_169_out, b1);
  not not_170 (not_170_out, b2);
  not not_171 (not_171_out, b0);
  not not_172 (not_172_out, b1);
  not not_173 (not_173_out, b3);
  not not_174 (not_174_out, a3);
  not not_175 (not_175_out, b0);
  not not_176 (not_176_out, b1);
  not not_177 (not_177_out, a0);
  not not_178 (not_178_out, a1);
  not not_179 (not_179_out, b3);
  not not_180 (not_180_out, a0);
  not not_181 (not_181_out, a1);
  not not_182 (not_182_out, a3);
  not not_183 (not_183_out, a0);
  not not_184 (not_184_out, a1);
  not not_185 (not_185_out, a3);
  not not_186 (not_186_out, a1);
  not not_187 (not_187_out, a3);
  not not_188 (not_188_out, b2);
  not not_189 (not_189_out, b3);
  not not_190 (not_190_out, a0);
  not not_191 (not_191_out, a3);
  not not_192 (not_192_out, b2);
  not not_193 (not_193_out, b3);
  not not_194 (not_194_out, a2);
  not not_195 (not_195_out, a3);
  not not_196 (not_196_out, b1);
  not not_197 (not_197_out, b3);
  not not_198 (not_198_out, a2);
  not not_199 (not_199_out, a3);
  not not_200 (not_200_out, b0);
  not not_201 (not_201_out, b3);
  not not_202 (not_202_out, a0);
  not not_203 (not_203_out, a1);
  not not_204 (not_204_out, a3);
  not not_205 (not_205_out, b1);
  not not_206 (not_206_out, b3);
  and and_6 (and_6_out, a0, not_207_out);
  not not_207 (not_207_out, b0);
  and and_7 (and_7_out, b0, not_208_out);
  not not_208 (not_208_out, a0);
  or or_1 (y1_2, a3, b3, and_1_out, and_2_out, and_3_out, and_4_out, and_5_out);
  and and_8 (and_8_out, not_1_out, not_2_out, not_3_out);
  and and_9 (and_9_out, not_4_out, not_5_out, not_6_out);
  and and_10 (and_10_out, not_7_out, not_8_out, not_9_out, not_10_out);
  and and_11 (and_11_out, not_11_out, not_12_out, not_13_out, not_14_out, not_15_out);
  and and_12 (and_12_out, not_16_out, not_17_out, not_18_out, not_19_out, not_20_out);
  and and_13 (and_13_out, a0, a3, b2, b3);
  and and_14 (and_14_out, a1, a3, b2, b3);
  and and_15 (and_15_out, a2, a3, b0, b3);
  and and_16 (and_16_out, a2, a3, b1, b3);
  and and_17 (and_17_out, a2, a3, b2, b3);
  and and_18 (and_18_out, a0, a1, a3, b1, b3);
  and and_19 (and_19_out, a1, a3, b0, b1, b3);
  and and_20 (and_20_out, not_21_out, not_22_out, not_23_out);
  and and_21 (and_21_out, not_24_out, not_25_out, not_26_out);
  and and_22 (and_22_out, not_27_out, not_28_out, not_29_out, not_30_out);
  and and_23 (and_23_out, not_31_out, not_32_out, not_33_out, not_34_out, not_35_out);
  and and_24 (and_24_out, not_36_out, not_37_out, not_38_out, not_39_out, not_40_out);
  and and_25 (and_25_out, a1, a2, b1, not_41_out);
  and and_26 (and_26_out, a1, b1, b2, not_42_out);
  and and_27 (and_27_out, a2, a3, b2, not_43_out);
  and and_28 (and_28_out, a2, b2, b3, not_44_out);
  and and_29 (and_29_out, not_45_out, not_46_out, not_47_out);
  and and_30 (and_30_out, not_48_out, not_49_out, not_50_out);
  and and_31 (and_31_out, a0, a1, a2, b0, not_51_out);
  and and_32 (and_32_out, a0, a1, a3, b0, not_52_out);
  and and_33 (and_33_out, a0, b0, b1, b2, not_53_out);
  and and_34 (and_34_out, a0, b0, b1, b3, not_54_out);
  and and_35 (and_35_out, a3, not_55_out, not_56_out, not_57_out);
  and and_36 (and_36_out, a3, not_58_out, not_59_out, not_60_out);
  and and_37 (and_37_out, b2, not_61_out, not_62_out, not_63_out);
  and and_38 (and_38_out, b3, not_64_out, not_65_out, not_66_out);
  and and_39 (and_39_out, b3, not_67_out, not_68_out, not_69_out);
  and and_40 (and_40_out, not_70_out, not_71_out, not_72_out, not_73_out);
  and and_41 (and_41_out, b2, not_74_out, not_75_out, not_76_out, not_77_out);
  and and_42 (and_42_out, not_78_out, not_79_out, not_80_out, not_81_out, not_82_out);
  and and_43 (and_43_out, a0, a2, b0, b2);
  and and_44 (and_44_out, a1, b2, b3, not_83_out);
  and and_45 (and_45_out, a2, a3, b1, not_84_out);
  and and_46 (and_46_out, a3, b2, b3, not_85_out);
  and and_47 (and_47_out, a1, a3, not_86_out, not_87_out);
  and and_48 (and_48_out, b1, b3, not_88_out, not_89_out);
  and and_49 (and_49_out, a0, a1, a2, b1, not_90_out);
  and and_50 (and_50_out, a0, a1, b0, b3, not_91_out);
  and and_51 (and_51_out, a0, a3, b0, b1, not_92_out);
  and and_52 (and_52_out, a1, b0, b1, b2, not_93_out);
  and and_53 (and_53_out, a2, not_94_out, not_95_out, not_96_out);
  and and_54 (and_54_out, b2, not_97_out, not_98_out, not_99_out);
  and and_55 (and_55_out, not_100_out, not_101_out, not_102_out, not_103_out);
  and and_56 (and_56_out, not_104_out, not_105_out, not_106_out, not_107_out);
  and and_57 (and_57_out, not_108_out, not_109_out, not_110_out, not_111_out);
  and and_58 (and_58_out, not_112_out, not_113_out, not_114_out, not_115_out);
  and and_59 (and_59_out, a0, b0, not_116_out, not_117_out, not_118_out);
  and and_60 (and_60_out, a0, b0, not_119_out, not_120_out, not_121_out);
  and and_61 (and_61_out, a1, not_122_out, not_123_out, not_124_out, not_125_out);
  and and_62 (and_62_out, a3, not_126_out, not_127_out, not_128_out, not_129_out);
  and and_63 (and_63_out, b1, not_130_out, not_131_out, not_132_out, not_133_out);
  and and_64 (and_64_out, b3, not_134_out, not_135_out, not_136_out, not_137_out);
  and and_65 (and_65_out, a1, b1, not_138_out, not_139_out, not_140_out, not_141_out);
  and and_66 (and_66_out, a2, a3, b2, b3);
  and and_67 (and_67_out, a0, b1, not_142_out, not_143_out);
  and and_68 (and_68_out, a1, b0, not_144_out, not_145_out);
  and and_69 (and_69_out, a0, a1, a2, b0, b1, b2);
  and and_70 (and_70_out, a1, not_146_out, not_147_out, not_148_out);
  and and_71 (and_71_out, b1, not_149_out, not_150_out, not_151_out);
  and and_72 (and_72_out, a0, a3, b1, not_152_out, not_153_out);
  and and_73 (and_73_out, a0, b2, b3, not_154_out, not_155_out);
  and and_74 (and_74_out, a2, a3, b0, not_156_out, not_157_out);
  and and_75 (and_75_out, b0, b1, b3, not_158_out, not_159_out);
  and and_76 (and_76_out, a0, a1, a3, b0, b1, not_160_out);
  and and_77 (and_77_out, a0, a1, b0, b1, b3, not_161_out);
  and and_78 (and_78_out, a0, a2, not_162_out, not_163_out, not_164_out);
  and and_79 (and_79_out, a0, b0, not_165_out, not_166_out, not_167_out);
  and and_80 (and_80_out, a0, b0, not_168_out, not_169_out, not_170_out);
  and and_81 (and_81_out, a1, a3, not_171_out, not_172_out, not_173_out);
  and and_82 (and_82_out, a1, b3, not_174_out, not_175_out, not_176_out);
  and and_83 (and_83_out, a3, b1, not_177_out, not_178_out, not_179_out);
  and and_84 (and_84_out, b0, b2, not_180_out, not_181_out, not_182_out);
  and and_85 (and_85_out, b1, b3, not_183_out, not_184_out, not_185_out);
  and and_86 (and_86_out, a0, not_186_out, not_187_out, not_188_out, not_189_out);
  and and_87 (and_87_out, a1, not_190_out, not_191_out, not_192_out, not_193_out);
  and and_88 (and_88_out, b0, not_194_out, not_195_out, not_196_out, not_197_out);
  and and_89 (and_89_out, b1, not_198_out, not_199_out, not_200_out, not_201_out);
  and and_90 (and_90_out, not_202_out, not_203_out, not_204_out, not_205_out, not_206_out);
  or or_2 (y0_0, and_6_out, and_7_out);
  or or_3 (y1_1, and_8_out, and_9_out, and_10_out, and_11_out, and_12_out);
  or or_4 (y1_0, and_13_out, and_14_out, and_15_out, and_16_out, and_17_out, and_18_out, and_19_out, and_20_out, and_21_out, and_22_out, and_23_out, and_24_out);
  or or_5 (y0_3, and_25_out, and_26_out, and_27_out, and_28_out, and_29_out, and_30_out, and_31_out, and_32_out, and_33_out, and_34_out, and_35_out, and_36_out, and_37_out, and_38_out, and_39_out, and_40_out, and_41_out, and_42_out);
  or or_6 (y0_2, and_43_out, and_44_out, and_45_out, and_46_out, and_47_out, and_48_out, and_49_out, and_50_out, and_51_out, and_52_out, and_53_out, and_54_out, and_55_out, and_56_out, and_57_out, and_58_out, and_59_out, and_60_out, and_61_out, and_62_out, and_63_out, and_64_out, and_65_out);
  or or_7 (y0_1, and_66_out, and_67_out, and_68_out, and_69_out, and_70_out, and_71_out, and_72_out, and_73_out, and_74_out, and_75_out, and_76_out, and_77_out, and_78_out, and_79_out, and_80_out, and_81_out, and_82_out, and_83_out, and_84_out, and_85_out, and_86_out, and_87_out, and_88_out, and_89_out, and_90_out);

  assign y1_3 = 1'b0;
endmodule

module _8_bit_Summer (
  input  [7:0] A,
  input  [7:0] B,
  output out_3,
  output [7:0] out_4
);

  wire n1_bit_summer_2_bout, n1_bit_summer_3_bout, n1_bit_summer_4_bout, n1_bit_summer_5_bout,
       n1_bit_summer_6_bout, n1_bit_summer_7_bout, n1_bit_summer_8_bout;

  _1_bit_Summer u_1_bit_summer_1 (.x1(A[7]), .x2(B[7]), .x3(n1_bit_summer_2_bout), .d(out_4[7]), .bout(out_3));
  _1_bit_Summer u_1_bit_summer_2 (
    .x1(A[6]), .x2(B[6]), .x3(n1_bit_summer_3_bout), .d(out_4[6]), .bout(n1_bit_summer_2_bout));
  _1_bit_Summer u_1_bit_summer_3 (
    .x1(A[5]), .x2(B[5]), .x3(n1_bit_summer_4_bout), .d(out_4[5]), .bout(n1_bit_summer_3_bout));
  _1_bit_Summer u_1_bit_summer_4 (
    .x1(A[4]), .x2(B[4]), .x3(n1_bit_summer_6_bout), .d(out_4[4]), .bout(n1_bit_summer_4_bout));
  _1_bit_Summer u_1_bit_summer_5 (
    .x1(A[2]), .x2(B[2]), .x3(n1_bit_summer_7_bout), .d(out_4[2]), .bout(n1_bit_summer_5_bout));
  _1_bit_Summer u_1_bit_summer_6 (
    .x1(A[3]), .x2(B[3]), .x3(n1_bit_summer_5_bout), .d(out_4[3]), .bout(n1_bit_summer_6_bout));
  _1_bit_Summer u_1_bit_summer_7 (
    .x1(A[1]), .x2(B[1]), .x3(n1_bit_summer_8_bout), .d(out_4[1]), .bout(n1_bit_summer_7_bout));
  _1_bit_Summer u_1_bit_summer_8 (.x1(A[0]), .x2(B[0]), .x3(1'b0), .d(out_4[0]), .bout(n1_bit_summer_8_bout));
endmodule
